# Fritzing sketch WordClock_v1 (saved by Fritzing 0.9.3b)

parts:
  S2 = Momentary Switch [part_number="Button B" package=ksa_sealed_tac_switch]
  S1 = Momentary Switch [part_number="Button A" package=ksa_sealed_tac_switch]
  ZS-042_RTC1 = ZS-042 RTC Module
  J1 = JST-B3P-VH [part_number="to WS2812" package=THT]
  WeMos_D1_Mini1 = WeMos D1 Mini

nets:
  GND: S2.2, S1.2, ZS-042_RTC1.GND, J1.pin3, WeMos_D1_Mini1.G
  N1: S2.3, WeMos_D1_Mini1.D6
  N2: S1.3, WeMos_D1_Mini1.D5
  5V: ZS-042_RTC1.VCC, WeMos_D1_Mini1.3V3
  N3: ZS-042_RTC1.SDA, WeMos_D1_Mini1.D2
  N4: ZS-042_RTC1.SCL, WeMos_D1_Mini1.D1
  N5: ZS-042_RTC1.SQW, WeMos_D1_Mini1.D7
  N6: J1.pin2, WeMos_D1_Mini1.D3
  N7: J1.pin1, WeMos_D1_Mini1.5V

notes:
  to WS2812 strip
